// Logisim project ALU.circ as structural Verilog: 2 circuits, main circuit main
module main (
  input  [2:0] ALUOp,
  input  [15:0] A,
  input  [15:0] B,
  input  Ainvert,
  input  Bnegate,
  input  [15:0] in_6,
  input  [15:0] in_7,
  output [15:0] Result,
  output [15:0] Result2,
  output GT,
  output Zero,
  output LT
);

  wire and_1_out, and_2_out, not_1_p2, not_3_out, or_1_p3, or_3_out;
  wire [14:0] multiplexer_1_p4;
  wire [15:0] adder_1_out, adder_2_out, BitWise_out, divider_1_rem, DivOut, MulOut, multiplexer_2_out,
       multiplier_1_cout, not_2_p2, not_4_out, not_5_out, Shift_Left, Shift_Right;

  // NOT_Gate #(.width(16)) not_1: pin names not known; wires that end beside it: A, not_1_p2
  // NOT_Gate #(.width(16)) not_2: pin names not known; wires that end beside it: B, not_2_p2
  // Multiplexer #(.width(16)) multiplexer_1: pin names not known; wires that end beside it: A, not_1_p2, Ainvert, {LT, multiplexer_1_p4}
  Multiplexer #(.width(16)) multiplexer_2 (
    .in0(B), .in1(not_2_p2), .out(multiplexer_2_out), .sel(Bnegate));  // open: en
  Multiplexer #(.width(16)) multiplexer_3 (.in1(multiplier_1_cout), .out(Result2), .sel(and_1_out));  // open: in0, en
  and and_1 (and_1_out, ALUOp[2], ~ALUOp[1], ~ALUOp[0]);  // AND_Gate
  not not_3 (not_3_out, Bnegate);
  Adder #(.width(16)) adder_1 (
    .a({LT, multiplexer_1_p4}), .b(multiplexer_2_out), .out(adder_1_out), .cin(Bnegate));  // open: cout
  // NOT_Gate not_4 has open pins: in=open, out=not_4_out
  // OR_Gate #(.width(16)) or_1: pin names not known; wires that end beside it: {LT, multiplexer_1_p4}, multiplexer_2_out, or_1_p3
  Shifter #(.width(16)) shifter_1 (.in(A), .\dist (B[3:0]), .out(Shift_Left));
  Multiplier #(.width(16)) multiplier_1 (.a(A), .b(B), .out(MulOut), .cout(multiplier_1_cout));  // open: cin
  Adder #(.width(16)) adder_2 (
    .a({LT, multiplexer_1_p4}), .b(not_4_out), .out(adder_2_out), .cin(not_3_out));  // open: cout
  assign BitWise_out = {LT, multiplexer_1_p4} & multiplexer_2_out;  // AND_Gate BitWise, 16 bits wide
  // NOT_Gate not_5 has open pins: in=open, out=not_5_out
  // OR_Gate or_2 has open pins: in0=B[4], in1=B[5], in2=B[6], in3=B[7], in4=B[8], in5=B[9], in6=B[10], in7=B[11], in8=B[12], in9=B[13], in10=B[14], in11=B[15], out=open
  or or_3 (or_3_out, multiplexer_1_p4[0], multiplexer_1_p4[1], multiplexer_1_p4[2], multiplexer_1_p4[3], multiplexer_1_p4[4], multiplexer_1_p4[5], multiplexer_1_p4[6], multiplexer_1_p4[7], multiplexer_1_p4[8], multiplexer_1_p4[9], multiplexer_1_p4[10], multiplexer_1_p4[11], multiplexer_1_p4[12], multiplexer_1_p4[13], multiplexer_1_p4[14]);
  Multiplexer #(.width(16)) multiplexer_4 (.in1(in_6));  // open: in0, out, sel, en
  Divider #(.width(16)) divider_1 (.a(A), .b(B), .out(DivOut), .rem(divider_1_rem));  // open: upper
  Multiplexer #(.width(16)) multiplexer_5 (.in1(divider_1_rem), .out(Result2), .sel(and_2_out));  // open: in0, en
  and and_2 (and_2_out, ALUOp[2], ~ALUOp[1], ALUOp[0]);  // AND_Gate
  and and_3 (GT, or_3_out, LT);
  // NOT_Gate not_6 has open pins: in=LT, out=open
  Multiplexer #(.select(3), .width(16)) multiplexer_6 (
    .in0(BitWise_out), .in1(not_5_out), .in2(adder_1_out), .in3(adder_2_out), .in4(MulOut), .in5(DivOut),
    .in6(Shift_Left), .in7(Shift_Right), .out(Result), .sel(ALUOp));  // open: en
  Shifter #(.width(16), .shift("lr")) shifter_2 (.in(A), .\dist (B[3:0]), .out(Shift_Right));
  // OR_Gate or_4 has open pins: in0=B[4], in1=B[5], in2=B[6], in3=B[7], in4=B[8], in5=B[9], in6=B[10], in7=B[11], in8=B[12], in9=B[13], in10=B[14], in11=B[15], out=open
  nor nor_1 (Zero, multiplexer_1_p4[0], multiplexer_1_p4[1], multiplexer_1_p4[2], multiplexer_1_p4[3], multiplexer_1_p4[4], multiplexer_1_p4[5], multiplexer_1_p4[6], multiplexer_1_p4[7], multiplexer_1_p4[8], multiplexer_1_p4[9], multiplexer_1_p4[10], multiplexer_1_p4[11], multiplexer_1_p4[12], multiplexer_1_p4[13], multiplexer_1_p4[14], LT);
  Multiplexer #(.width(16)) multiplexer_7 (.in1(in_7));  // open: in0, out, sel, en

  // Notes on the sheet:
  //   Inputs
  //   Shift Left Logic
  //   Design your ALU in this file
  //   A - First ALU input
  //   B - Second ALU input
  //   Result - ALU main result
  //   Result2 - Output for MSB of mul/div operations
  //   GT/Zero/LT - Comparison of input A with zero
  //    Don't modify any of the inputs/outputs in this file!
  //   ALUOp - The control signal defining the behaviour of the ALU
  //   Outputs
  //   Shift Right Logic
endmodule

module test (
  input  [2:0] in_1,
  input  [15:0] in_2,
  input  [15:0] in_3,
  output [15:0] out_4
);

  main main_1 (
    .ALUOp(in_1), .A(in_2), .B(in_3), .Result(out_4));  // open: GT, Zero, LT, Result2, Ainvert, Bnegate, in_6, in_7

  // Notes on the sheet:
  //   Test your circuit!
endmodule
