// Logisim project RegFile.circ as structural Verilog: 2 circuits, main circuit main
module main (
  input  [15:0] WriteData0,
  input  [15:0] WriteData1,
  input  [2:0] WriteSelect0,
  input  [2:0] ReadSelect0,
  input  [2:0] ReadSelect1,
  input  WE0,
  input  WE1,
  input  Clock,
  output [15:0] Reg0,
  output [15:0] Reg1,
  output [15:0] Reg2,
  output [15:0] Reg3,
  output [15:0] Reg4,
  output [15:0] Reg5,
  output [15:0] Reg6,
  output [15:0] Reg7,
  output [15:0] ReadData0,
  output [15:0] ReadData1
);

  wire and_9_p4, and_10_p3, and_11_out, and_12_out, and_13_p3, and_14_p3, and_15_p3, and_16_out,
       decoder_1_out0, decoder_1_out1, decoder_1_out2, decoder_1_out3, decoder_1_out4, decoder_1_out5,
       decoder_1_out6, decoder_1_out7, demultiplexer_1_out0, demultiplexer_1_out1, demultiplexer_1_out2,
       demultiplexer_1_out3, demultiplexer_1_out4, demultiplexer_1_out5, demultiplexer_1_out6,
       demultiplexer_1_out7, or_1_out, or_2_out, or_3_out, or_4_out, or_5_out, or_6_out, or_7_out, or_8_out,
       SelReg0, SelReg1, SelReg2, SelReg3, SelReg4, SelReg5, SelReg6, SelReg7;
  wire [2:0] adder_1_out;
  wire [15:0] multiplexer_1_out, multiplexer_2_out, multiplexer_3_out, multiplexer_4_out, multiplexer_5_out,
       multiplexer_6_out, multiplexer_7_out, multiplexer_8_out;

  Demultiplexer #(.select(3)) demultiplexer_1 (
    .out0(demultiplexer_1_out0), .out1(demultiplexer_1_out1), .out2(demultiplexer_1_out2),
    .out3(demultiplexer_1_out3), .out4(demultiplexer_1_out4), .out5(demultiplexer_1_out5),
    .out6(demultiplexer_1_out6), .out7(demultiplexer_1_out7), .in(1'b1), .sel(adder_1_out));  // open: en
  Adder #(.width(3)) adder_1 (.a(WriteSelect0), .b(3'b001), .out(adder_1_out));  // open: cin, cout
  Decoder #(.select(3)) decoder_1 (
    .out0(decoder_1_out0), .out1(decoder_1_out1), .out2(decoder_1_out2), .out3(decoder_1_out3),
    .out4(decoder_1_out4), .out5(decoder_1_out5), .out6(decoder_1_out6), .out7(decoder_1_out7),
    .sel(WriteSelect0));  // open: en
  and and_1 (SelReg0, decoder_1_out0, WE0);
  and and_2 (SelReg1, WE0, decoder_1_out1);
  and and_3 (SelReg2, decoder_1_out2, WE0);
  and and_4 (SelReg3, decoder_1_out3, WE0);
  and and_5 (SelReg4, decoder_1_out4, WE0);
  and and_6 (SelReg5, decoder_1_out5, WE0);
  and and_7 (SelReg6, decoder_1_out6, WE0);
  and and_8 (SelReg7, decoder_1_out7, WE0);
  // AND_Gate and_9: pin names not known; wires that end beside it: WE1, WE1, demultiplexer_1_out0, and_9_p4
  // AND_Gate and_10: pin names not known; wires that end beside it: WE1, demultiplexer_1_out1, and_10_p3
  and and_11 (and_11_out, WE1, demultiplexer_1_out2);
  and and_12 (and_12_out, WE1, demultiplexer_1_out3);
  // AND_Gate and_13: pin names not known; wires that end beside it: WE1, demultiplexer_1_out4, and_13_p3
  // AND_Gate and_14: pin names not known; wires that end beside it: WE1, demultiplexer_1_out5, and_14_p3
  or or_1 (or_1_out, SelReg6, and_15_p3);
  // AND_Gate and_15: pin names not known; wires that end beside it: WE1, demultiplexer_1_out6, and_15_p3
  or or_2 (or_2_out, SelReg7, and_16_out);
  and and_16 (and_16_out, SelReg7, WE1, demultiplexer_1_out7);
  or or_3 (or_3_out, SelReg0, and_9_p4);
  or or_4 (or_4_out, SelReg1, and_10_p3);
  or or_5 (or_5_out, SelReg2, SelReg2, and_11_out);
  or or_6 (or_6_out, SelReg3, SelReg3, and_12_out);
  or or_7 (or_7_out, SelReg4, and_13_p3);
  or or_8 (or_8_out, SelReg5, and_14_p3);
  Multiplexer #(.width(16)) multiplexer_1 (
    .in0(WriteData0), .in1(WriteData1), .out(multiplexer_1_out), .sel(and_10_p3));  // open: en
  Multiplexer #(.width(16)) multiplexer_2 (
    .in0(WriteData0), .in1(WriteData1), .out(multiplexer_2_out), .sel(and_11_out));  // open: en
  Multiplexer #(.width(16)) multiplexer_3 (
    .in0(WriteData0), .in1(WriteData1), .out(multiplexer_3_out), .sel(and_12_out));  // open: en
  Multiplexer #(.width(16)) multiplexer_4 (
    .in0(WriteData0), .in1(WriteData1), .out(multiplexer_4_out), .sel(and_13_p3));  // open: en
  Multiplexer #(.width(16)) multiplexer_5 (
    .in0(WriteData0), .in1(WriteData1), .out(multiplexer_5_out), .sel(and_14_p3));  // open: en
  Multiplexer #(.width(16)) multiplexer_6 (
    .in0(WriteData0), .in1(WriteData1), .out(multiplexer_6_out), .sel(and_15_p3));  // open: en
  Multiplexer #(.width(16)) multiplexer_7 (
    .in0(WriteData0), .in1(WriteData1), .out(multiplexer_7_out), .sel(and_16_out));  // open: en
  Multiplexer #(.width(16)) multiplexer_8 (
    .in0(WriteData0), .in1(WriteData1), .out(multiplexer_8_out), .sel(and_9_p4));  // open: en
  Register #(.width(16), .trigger("falling")) register_1 (
    .D(multiplexer_8_out), .en(or_3_out), .Q(Reg0), .clk(Clock));  // open: clr
  Register #(.width(16), .trigger("falling")) register_2 (
    .D(multiplexer_1_out), .en(or_4_out), .Q(Reg1), .clk(Clock));  // open: clr
  Register #(.width(16), .trigger("falling")) register_3 (
    .D(multiplexer_2_out), .en(or_5_out), .Q(Reg2), .clk(Clock));  // open: clr
  Register #(.width(16), .trigger("falling")) register_4 (
    .D(multiplexer_3_out), .en(or_6_out), .Q(Reg3), .clk(Clock));  // open: clr
  Register #(.width(16), .trigger("falling")) register_5 (
    .D(multiplexer_4_out), .en(or_7_out), .Q(Reg4), .clk(Clock));  // open: clr
  Register #(.width(16), .trigger("falling")) register_6 (
    .D(multiplexer_5_out), .en(or_8_out), .Q(Reg5), .clk(Clock));  // open: clr
  Register #(.width(16), .trigger("falling")) register_7 (
    .D(multiplexer_6_out), .en(or_1_out), .Q(Reg6), .clk(Clock));  // open: clr
  Register #(.width(16), .trigger("falling")) register_8 (
    .D(multiplexer_7_out), .en(or_2_out), .Q(Reg7), .clk(Clock));  // open: clr
  Multiplexer #(.select(3), .width(16)) multiplexer_9 (
    .in0(Reg0), .in1(Reg1), .in2(Reg2), .in3(Reg3), .in4(Reg4), .in5(Reg5), .in6(Reg6), .in7(Reg7),
    .out(ReadData1), .sel(ReadSelect1));  // open: en
  Multiplexer #(.select(3), .width(16)) multiplexer_10 (
    .in0(Reg0), .in1(Reg1), .in2(Reg2), .in3(Reg3), .in4(Reg4), .in5(Reg5), .in6(Reg6), .in7(Reg7),
    .out(ReadData0), .sel(ReadSelect0));  // open: en

  // Other names for the same wires on the sheet: WriteEnable0 = WE0; WriteEnable1 = WE1

  // Notes on the sheet:
  //   Inputs
  //   Add the registers to this file
  //   WriteSelect0 - Register to write to
  //   WE0 - Enable writing to 1 register
  //   ReadSelect0 - First register to read data from
  //   ReadSelect1 - Second register to read data from
  //   WE1 - Enable writing to 2nd register (mul/div)
  //   ReadData0 - Data being read from first register
  //   ReadData1 - Data being read from second register
  //   WriteData0 - The data to be written to register by most instructions
  //   WriteData1 - The data to be written to second register by mul/div
  //   These can be used for debug and testing
  //   and design the logic to control them
  //    Don't modify any of the inputs/outputs in this file!
  //   Outputs
endmodule

module test (
  input  [15:0] Write_data_A,
  input  Write_Enable_Port_A,
  input  [2:0] in_3,
  input  [15:0] Write_data_B,
  input  Write_Enable_Port_B,
  input  [2:0] Select_Read_A,
  input  [2:0] Select_Read_B
);

  wire Clock_out;
  wire [15:0] main_1_readdata0, main_1_readdata1, main_1_reg0, main_1_reg1, main_1_reg2, main_1_reg3,
       main_1_reg4, main_1_reg5, main_1_reg6, main_1_reg7;

  // Probe on main_1_reg1
  // Probe on main_1_reg0
  // Probe on main_1_reg3
  // Probe on main_1_reg2
  Button Clock (.out(Clock_out));
  // Probe on main_1_reg4
  // Probe on main_1_reg5
  // Probe on main_1_reg6
  // Probe on main_1_reg7
  main main_1 (
    .WriteData0(Write_data_A), .WriteData1(Write_data_B), .ReadData0(main_1_readdata0),
    .ReadData1(main_1_readdata1), .WriteSelect0(in_3), .ReadSelect0(Select_Read_A),
    .ReadSelect1(Select_Read_B), .Reg0(main_1_reg0), .Reg1(main_1_reg1), .Reg2(main_1_reg2),
    .Reg3(main_1_reg3), .Reg4(main_1_reg4), .Reg5(main_1_reg5), .Reg6(main_1_reg6), .Reg7(main_1_reg7),
    .WE0(Write_Enable_Port_A), .WE1(Write_Enable_Port_B), .Clock(Clock_out));
  // Probe on main_1_readdata0
  // Probe on main_1_readdata1

  // Notes on the sheet:
  //   Test your circuit!
endmodule
