// Logisim project ALU.circ as structural Verilog: 2 circuits, main circuit main
module main (
  input  [2:0] ALUOp,
  input  [15:0] A,
  input  [15:0] B,
  output [15:0] Result,
  output [15:0] Result2,
  output GT,
  output Zero,
  output LT
);


  // Notes on the sheet:
  //   Inputs
  //   Design your ALU in this file
  //   A - First ALU input
  //   B - Second ALU input
  //   Result - ALU main result
  //    Don't modify any of the inputs/outputs in this file!
  //   ALUOp - The control signal defining the behaviour of the ALU
  //   Result2 - Output for MSB of mul/div operations
  //   GT/Zero/LT - Comparison of input A with zero
  //   Outputs
endmodule

module test (
);

  main main_1 ();  // open: ALUOp, A, B, Result, GT, Zero, LT, Result2

  // Notes on the sheet:
  //   Test your circuit!
endmodule
