// Logisim project umips.circ as structural Verilog: 3 circuits, main circuit main
module main (
  input  Reset,
  output [15:0] Reg0,
  output [15:0] Reg1,
  output [15:0] Reg2,
  output [15:0] Reg3,
  output [15:0] Reg4,
  output [15:0] Reg5,
  output [15:0] Reg6,
  output [15:0] Reg7,
  output [3:0] Output3,
  output [3:0] Output2,
  output [3:0] Output1,
  output [3:0] Output0,
  output halt
);

  wire ALUBMux, and_1_out, Clock, GT, load, LT, PutEnable, store, Subop, WriteEn0, WriteEn1, Z;
  wire [1:0] WriteEn0Con;
  wire [2:0] ALUOp, J_br_next, Rs, Rt;
  wire [4:0] Opcode_Subop;
  wire [7:0] CurIn, Imm, multiplexer_2_out, multiplexer_4_out, multiplexer_5_out, multiplexer_7_out,
       multiplexer_8_out, PC_1;
  wire [15:0] bit_extender_1_out, bit_extender_2_out, bit_extender_3_out, bit_extender_4_out, CurIns, DataRA,
       DataRB, ExtImm, multiplexer_1_out, multiplexer_3_out, Result, Result2, WMemtoRs;

  Clock clock_1 (.out(Clock));
  and and_1 (and_1_out, ~1'b1, halt);  // AND_Gate
  InsDecoder Instruction_Decoder (
    .Instruction(CurIns), .Opcode_Subop(Opcode_Subop), .Subop(Subop), .Rt(Rt), .Rs(Rs), .Immediate(Imm));  // open: Unused
  Register #(.width(16), .trigger("falling")) register_1 (
    .D(DataRA), .en(PutEnable), .Q({Output3, Output2, Output1, Output0}), .clk(Clock));  // open: clr
  Counter #(.ongoal("stay"), .trigger("falling")) PC (
    .load(and_1_out), .D(multiplexer_8_out), .count(1'b0), .Q(CurIn), .clk(Clock), .clr(Reset));  // open: carry
  Control control_1 (
    .Opcode_Subop(Opcode_Subop), .J_br_next_select(J_br_next), .ALUop(ALUOp), .Halt(halt),
    .Put_Enable(PutEnable), .Enable_Write_0(WriteEn0), .Enable_Write_1(WriteEn1), .Load(load), .Store(store),
    .WriteData0Control(WriteEn0Con), .ALU_B_Mux(ALUBMux));  // open: Immediate
  assign bit_extender_1_out = {{8{1'b0}}, PC_1};  // Bit_Extender bit_extender_1
  assign bit_extender_2_out = {{8{1'b0}}, Imm};  // Bit_Extender bit_extender_2
  Multiplexer #(.select(2), .width(16)) multiplexer_1 (
    .in0(Result), .in1(bit_extender_1_out), .in2(bit_extender_2_out), .in3(WMemtoRs),
    .out(multiplexer_1_out), .sel(WriteEn0Con));  // open: en
  Adder adder_1 (.a(CurIn), .b(8'h1), .out(PC_1));  // open: cin, cout
  Multiplexer #(.width(8)) multiplexer_2 (.in0(PC_1), .in1(Imm), .out(multiplexer_2_out), .sel(LT));  // open: en
  ALU_main main_1 (
    .ALUOp(ALUOp), .A(DataRA), .B(multiplexer_3_out), .Result(Result), .GT(GT), .Zero(Z), .LT(LT),
    .Result2(Result2));
  Multiplexer #(.width(16)) multiplexer_3 (
    .in0(DataRB), .in1(ExtImm), .out(multiplexer_3_out), .sel(ALUBMux));  // open: en
  assign bit_extender_3_out = {{8{1'b0}}, Imm};  // Bit_Extender bit_extender_3
  assign bit_extender_4_out = {{8{Imm[7]}}, Imm};  // Bit_Extender bit_extender_4
  Multiplexer #(.width(8)) multiplexer_4 (.in0(Imm), .in1(PC_1), .out(multiplexer_4_out), .sel(Z));  // open: en
  RegFile_main main_2 (
    .WriteData0(multiplexer_1_out), .WriteData1(Result2), .ReadData0(DataRA), .ReadData1(DataRB),
    .WriteSelect0(Rs), .ReadSelect0(Rs), .ReadSelect1(Rt), .Reg0(Reg0), .Reg1(Reg1), .Reg2(Reg2),
    .Reg3(Reg3), .Reg4(Reg4), .Reg5(Reg5), .Reg6(Reg6), .Reg7(Reg7), .WE0(WriteEn0), .WE1(WriteEn1),
    .Clock(Clock));
  Multiplexer #(.width(8)) multiplexer_5 (.in0(PC_1), .in1(Imm), .out(multiplexer_5_out), .sel(Z));  // open: en
  Multiplexer #(.width(16)) multiplexer_6 (
    .in0(bit_extender_3_out), .in1(bit_extender_4_out), .out(ExtImm), .sel(Subop));  // open: en
  Multiplexer #(.width(8)) multiplexer_7 (.in0(PC_1), .in1(Imm), .out(multiplexer_7_out), .sel(GT));  // open: en
  Multiplexer #(.select(3), .width(8)) multiplexer_8 (
    .in0(PC_1), .in1(DataRA[7:0]), .in2(Imm), .in3(Imm), .in4(multiplexer_2_out), .in5(multiplexer_4_out),
    .in6(multiplexer_5_out), .in7(multiplexer_7_out), .out(multiplexer_8_out), .sel(J_br_next));  // open: en
  ROM #(.dataWidth(16)) rom_1 (.addr(CurIn), .data(CurIns), .sel(1'b1));
  Hex_Digit_Display hex_digit_display_1 (.value(Output3));  // open: dp
  LED led_1 (.in(halt));
  Hex_Digit_Display hex_digit_display_2 (.value(Output2));  // open: dp
  RAM #(.dataWidth(16), .bus("separate")) ram_1 (
    .addr(DataRB[7:0]), .din(DataRA), .data(WMemtoRs), .str(store), .sel(1'b1), .clk(Clock), .ld(load),
    .clr(Reset));
  Hex_Digit_Display hex_digit_display_3 (.value(Output1));  // open: dp
  Hex_Digit_Display hex_digit_display_4 (.value(Output0));  // open: dp

  // Notes on the sheet:
  //   Regfile WriteData0 Select Mux
  //    Don't modify these, they are used for debug and testing
  //   ALU B Op Mux
  //   Zero Extender
  //   Sign Extender
  //   Design your CPU in this file
  //   You must connect Reg0..7 to the top ports of the register file.
  //   Include everything here (ALU, RegFile, Control, PC, RAM, ROM, LEDs, Displays, ...)
  //   ROM
  //   Branch/Jump/next Mux
  //   <-- Handle J and Branches 
  //   Connect Output3..0 to your LED display.
  //   Output3 is the most significant
  //   RAM
  //   Connect halt to your halt LED
endmodule

module InsDecoder (
  input  [15:0] Instruction,
  output [4:0] Opcode_Subop,
  output Subop,
  output [4:0] Unused,
  output [2:0] Rt,
  output [2:0] Rs,
  output [7:0] Immediate
);


  assign Immediate = Instruction[8:1];
  assign Opcode_Subop = {Instruction[15:12], Instruction[0]};
  assign Rs = Instruction[11:9];
  assign Rt = Instruction[8:6];
  assign Subop = Instruction[0];
  assign Unused = Instruction[5:1];
endmodule

module Control (
  input  [4:0] Opcode_Subop,
  input  [7:0] Immediate,
  output [2:0] J_br_next_select,
  output [2:0] ALUop,
  output Halt,
  output Put_Enable,
  output Enable_Write_0,
  output Enable_Write_1,
  output Load,
  output Store,
  output [1:0] WriteData0Control,
  output ALU_B_Mux
);

  wire add, addi, addui, \and , bn, bp, bx, bz, decoder_1_out8, decoder_1_out9, decoder_1_out11,
       decoder_1_out16, decoder_1_out17, decoder_1_out18, decoder_1_out19, decoder_1_out20, decoder_1_out21,
       decoder_1_out22, decoder_1_out23, decoder_1_out24, decoder_1_out25, decoder_1_out26, decoder_1_out27,
       decoder_1_out28, decoder_1_out29, decoder_1_out30, decoder_1_out31, div, j, jal, jr, li, mul, \nor ,
       or_10_out, sllv, srlv, sub, undriven, undriven_2, undriven_3, undriven_4, undriven_5, undriven_6;

  Decoder #(.select(5)) decoder_1 (
    .out0(add), .out1(sub), .out2(\nor ), .out3(\and ), .out4(mul), .out5(div), .out6(addui), .out7(addi),
    .out8(decoder_1_out8), .out9(decoder_1_out9), .out10(li), .out11(decoder_1_out11), .out12(srlv),
    .out13(sllv), .out14(Store), .out15(Load), .out16(decoder_1_out16), .out17(decoder_1_out17),
    .out18(decoder_1_out18), .out19(decoder_1_out19), .out20(decoder_1_out20), .out21(decoder_1_out21),
    .out22(decoder_1_out22), .out23(decoder_1_out23), .out24(decoder_1_out24), .out25(decoder_1_out25),
    .out26(decoder_1_out26), .out27(decoder_1_out27), .out28(decoder_1_out28), .out29(decoder_1_out29),
    .out30(decoder_1_out30), .out31(decoder_1_out31), .sel(Opcode_Subop));  // open: en
  or or_1 (bp, decoder_1_out8, decoder_1_out9);
  or or_2 (Put_Enable, decoder_1_out16, decoder_1_out17, undriven_2);
  or or_3 (Halt, undriven_2, decoder_1_out18, decoder_1_out19, undriven_3);
  or or_4 (jal, undriven_3, decoder_1_out20, decoder_1_out21, undriven_4);
  or or_5 (j, undriven_4, decoder_1_out22, decoder_1_out23, undriven_5);
  or or_6 (bn, undriven_5, decoder_1_out24, decoder_1_out25, undriven_6);
  or or_7 (bx, undriven_6, decoder_1_out26, decoder_1_out27);
  or or_8 (jr, decoder_1_out28, decoder_1_out29, undriven);
  or or_9 (bz, undriven, decoder_1_out30, decoder_1_out31);
  or or_10 (or_10_out, add, addi, addui);
  Priority_Encoder priority_encoder_1 (
    .in0(1'b1), .in1(jr), .in2(j), .in3(jal), .in4(bn), .in5(bx), .in6(bz), .in7(bp), .out(J_br_next_select));  // open: en_in, gs, en_out
  Priority_Encoder priority_encoder_2 (
    .in0(1'b1), .in1(\nor ), .in2(or_10_out), .in3(sub), .in4(mul), .in5(div), .in6(sllv), .in7(srlv),
    .out(ALUop));  // open: en_in, gs, en_out
  or or_11 (Enable_Write_1, mul, div);
  or or_12 (ALU_B_Mux, addi, addui);
  Priority_Encoder #(.select(2)) priority_encoder_3 (
    .in0(1'b1), .in1(jal), .in2(li), .in3(Load), .out(WriteData0Control));  // open: gs, en_out, en_in
  or or_13 (Enable_Write_0, \and , add, mul, div, \nor , sub, addui, addi, li, srlv, sllv, Load, jal);

  // Other names for the same wires on the sheet: lw = Load; put = Put_Enable; sw = Store

  // Notes on the sheet:
  //   Default is next instruction
  //   J/br/next mux selector
  //   Default Op is Bit AND
  //   ALUop Enc
  //   Default is ALU result
endmodule
